# Fritzing sketch Ultrasonic_security (saved by Fritzing 0.9.3b)
breadboards: 1

parts:
  Part1 = Arduino Nano (Rev3.0)
  VCC1 = Battery
  LED1 = LED - 5mm [color="White (6500K)" package="5 mm [THT]"]
  R1 = Resistor [tolerance=±5% resistance=1k package=THT]
  hc-sr1 = hc-sr04
  J1 = Piezo Speaker

nets:
  N1: Part1.D1/TX, Part1.D12/MISO
  N2: Part1.RESET, VCC1.-, R1.Pin_1, hc-sr1.GND, J1.pin1
  N3: Part1.D3, hc-sr1.Echo
  N4: Part1.D11/MOSI, J1.pin2
  5V: Part1.5V, VCC1.+, hc-sr1.VCC
  N5: LED1.anode, R1.Pin_0

// code stored in the sketch: Sonar_security.ino
int tiger = 2;
int echo = 3;
//int a=12;
int ledPin = 12;
double Duration, Distance;

void setup()
{
  pinMode(tiger, OUTPUT);
  pinMode(echo, INPUT);
  Serial.begin(9600);
  // pinMode(a,OUTPUT);
  pinMode(ledPin, OUTPUT);
}
void loop()
{
  digitalWrite(tiger, HIGH);
  delayMicroseconds(1000);
  digitalWrite(tiger, LOW);
  Duration = pulseIn(echo, HIGH);
  Distance = (Duration / 2.0) / 29.1;
  Serial.print("\ncm = ");
  Serial.print(Distance);
  //delay(500);
  if (Distance < 150.0)
  {
    digitalWrite(ledPin, HIGH);
    delay(1000);
  }
  else
    digitalWrite(ledPin, LOW);
  delay(200);

}
